// Logisim project Mux.circ as structural Verilog: 3 circuits, main circuit main
module main (
  input  A,
  input  B,
  input  C,
  output X,
  output Y
);

  wire not_1_out;

  not not_1 (not_1_out, C);
  Mux4x1 mux4x1_1 (.\D₀ (1'b0), .\D₁ (C), .\D₂ (not_1_out), .\D₃ (1'b1), .S({A, B}), .Y(X));
  Mux4x1 mux4x1_2 (.\D₀ (1'b1), .\D₁ (not_1_out), .\D₂ (1'b0), .\D₃ (C), .S({A, B}), .Y(Y));

  // Other names for the same wires on the sheet: S[1:0] = {A, B}
endmodule

module Mux4x1 (
  input  [1:0] S,
  input  \D₀ ,
  input  \D₁ ,
  input  \D₂ ,
  input  \D₃ ,
  output Y
);

  wire and_1_out, and_2_out, and_3_out, and_4_out;

  and and_1 (and_1_out, \D₀ , ~S[1], ~S[0]);  // AND_Gate
  and and_2 (and_2_out, \D₁ , ~S[1], S[0]);  // AND_Gate
  and and_3 (and_3_out, \D₂ , S[1], ~S[0]);  // AND_Gate
  and and_4 (and_4_out, \D₃ , S[1], S[0]);
  or or_1 (Y, and_1_out, and_2_out, and_3_out, and_4_out);
endmodule

module Mux8x1 (
  input  S_36fa348e,
  input  S_0e805c6e,
  input  S_de45d96e,
  input  D_d2348313,
  input  D_d72e01c3,
  input  D_c6ac26ca,
  input  D_45745a7c,
  input  D_7ba976b1,
  input  D_75a2c752,
  input  D_8d387635,
  input  D_a17283b4,
  output Y
);

  wire and_1_out, and_2_out, and_3_out, and_4_out, and_5_out, and_6_out, and_7_out, and_8_out;

  and and_1 (and_1_out, D_d2348313, ~S_36fa348e, ~S_0e805c6e, ~S_de45d96e);  // AND_Gate
  and and_2 (and_2_out, D_d72e01c3, ~S_36fa348e, ~S_0e805c6e, S_de45d96e);  // AND_Gate
  and and_3 (and_3_out, D_c6ac26ca, ~S_36fa348e, S_0e805c6e, ~S_de45d96e);  // AND_Gate
  and and_4 (and_4_out, D_45745a7c, ~S_36fa348e, S_0e805c6e, S_de45d96e);  // AND_Gate
  and and_5 (and_5_out, D_7ba976b1, S_36fa348e, ~S_0e805c6e, ~S_de45d96e);  // AND_Gate
  and and_6 (and_6_out, D_75a2c752, S_36fa348e, ~S_0e805c6e, S_de45d96e);  // AND_Gate
  and and_7 (and_7_out, D_8d387635, S_36fa348e, S_0e805c6e, ~S_de45d96e);  // AND_Gate
  and and_8 (and_8_out, D_a17283b4, S_36fa348e, S_0e805c6e, S_de45d96e);
  or or_1 (Y, and_1_out, and_2_out, and_3_out, and_4_out, and_5_out, and_6_out, and_7_out, and_8_out);
endmodule
